# Fritzing sketch SpectroMeter2 (saved by Fritzing 1.0.5)
breadboards: 1

parts:
  Part1 = Arduino Nano (Rev3.0)
  R1 = Resistor [tolerance=±5% power=0.25W resistance=10k package=THT]
  R2 = Resistor [tolerance=±5% power=0.25W resistance=10k package=THT]
  R3 = Resistor [tolerance=±5% power=0.25W resistance=10k package=THT]
  R4 = Resistor [tolerance=±5% power=0.25W resistance=10k package=THT]
  LED2 = LED - 5mm [color="White (4500K)" current=0.030A part_number=L-53P3C package="5 mm [THT]"]
  LED3 = LED - 5mm [color="White (4500K)" current=0.030A part_number=L-53P3C package="5 mm [THT]"]
  LED4 = LED - 5mm [color="White (4500K)" current=0.030A part_number=L-53P3C package="5 mm [THT]"]
  LED5 = LED - 5mm [color="White (4500K)" current=0.030A part_number=L-53P3C package="5 mm [THT]"]
  R5 = Resistor [tolerance=±5% power=0.25W resistance=100 package=THT]
  R6 = Resistor [tolerance=±5% power=0.25W resistance=100 package=THT]
  R7 = Resistor [tolerance=±5% power=0.25W resistance=100 package=THT]
  R8 = Resistor [tolerance=±5% power=0.25W resistance=100 package=THT]
  R9 = Resistor [tolerance=±5% power=0.25W resistance=100 package=THT]
  R10 = Resistor [tolerance=±5% power=0.25W resistance=100 package=THT]
  LED6 = LED - 5mm [color="Infrared (940nm)" current=0.030A part_number="IR LED Transmitter" package="5 mm [THT]"]
  LED7 = RGB LED (com. cathode, rgb) [color="Red (633nm)" current=0.030A part_number="common Cathode RGB" package="5 mm [THT]"]
  LED8 = LED - 5mm [color="Yellow (574nm)" current=0.030A part_number="Yellow LED Translucent" package="5 mm [THT]"]
  LED9 = LED - 5mm [color="Orange (605nm)" current=0.030A part_number="Orange LED Translucent" package="5 mm [THT]"]

nets:
  N1: Part1.GND, R1.Pin_0, R2.Pin_0, R3.Pin_0, R4.Pin_0, LED6.cathode, LED7.common_cathode, LED8.cathode, LED9.cathode
  N2: Part1.D2, R5.Pin_1
  N3: Part1.D3, R6.Pin_1
  N4: Part1.D4, R7.Pin_1
  N5: Part1.D5, R8.Pin_1
  N6: Part1.D6, R9.Pin_1
  N7: Part1.D7, R10.Pin_1
  N8: Part1.5V, LED2.anode, LED3.anode, LED4.anode, LED5.anode
  N9: Part1.A3, R4.Pin_1, LED5.cathode
  N10: Part1.A2, R3.Pin_1, LED4.cathode
  N11: Part1.A1, R2.Pin_1, LED3.cathode
  N12: Part1.A0, R1.Pin_1, LED2.cathode
  N13: R5.Pin_0, LED7.blue_anode
  N14: R6.Pin_0, LED7.green_anode
  N15: R7.Pin_0, LED8.anode
  N16: R8.Pin_0, LED9.anode
  N17: R9.Pin_0, LED7.red_anode
  N18: R10.Pin_0, LED6.anode

notes:
  10 kOhm
  100 Ohm
  Arduino Nano V3
  4x L-53P3C
  RGB | Y | O | IR
